# Fritzing sketch Wiring (saved by Fritzing 1.0.5)
breadboards: 1

parts:
  U1 = ESP32S-HiLetgo [part_number=ESP32S-HiLetgo]
  S1 = H-Bridge with L298N
  SG1 = Buzzer 12mm [part_number=COM-07950 package=buzzer-12mm-ns]
  LED1 = LEDs [package=led10mm]
  M1 = gear-motor
  M2 = gear-motor
  R1 = Resistor [tolerance=±5% resistance=220 package="2512 [SMD]"]
  M5 = gear-motor
  M6 = gear-motor
  VCC1 = Battery [internal_resistance=0.1Ω]

nets:
  N1: U1.GPIO32, S1.ENA, S1.ENA-5V
  N2: U1.GPIO33, S1.IN4
  N3: U1.GPIO25, S1.IN3
  N4: U1.GPIO26, S1.IN2
  N5: U1.GPIO27, S1.IN1
  N6: U1.GPIO14, S1.ENB, S1.ENB-5V
  N7: U1.GND, SG1.2, LED1.C
  N8: U1.GPIO11, S1.GND, VCC1.-
  VIN: U1.VIN, S1.5V
  N9: U1.GPIO18, R1.Pin_0
  N10: U1.GPIO19, SG1.1
  N11: S1.12V, VCC1.+
  N12: S1.M1-01, M1.pin_2, M2.pin_2
  N13: S1.M1-02, M1.pin_1, M2.pin_1
  N14: S1.M2-01, M5.pin_2, M6.pin_2
  N15: S1.M2-02, M5.pin_1, M6.pin_1
  N16: LED1.A, R1.Pin_1

custom parts:
  ESP32S-HiLetgo: HiLetgo ESP-WROOM-32 ESP32 ESP-32S Development Board 2.4GHz Dual-Mode WiFi + Bluetooth Dual Cores Microcontroller The ESP32 integrated with Antenna switches, RF Balun, power amplifiers, low-noise amplifiers, filters, and management modules, and the entire solution occupies the least area of PCB. 2.4 GHz Wi-Fi plus Bluetooth dual-mode chip, with TSMC Ultra-low power consumption 40nm technology,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
  H-Bridge with L298N: h-bridge
  Buzzer 12mm: Buzzer 12mm Spark Fun Electronics SKU : Comp-Buzzer Through hole This is a small 12mm round speaker that operates around the audible 2kHz range. You can use these speakers to create simple music or user interfaces. This is not a true piezoelectric speaker but behaves similarly. Instead of a piezoelectric crystal that vibrates with an electric current, this tiny speaker uses an electromagnet to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
